# Fritzing sketch Button (saved by Fritzing 0.7.12b)
breadboards: 1

parts:
  R1 = Resistor [resistance=10k tolerance=±5% package=THT]
  Arduino2 = Arduino
  R2 = Rotary Potentiometer (Small) [maximum_resistance=100kΩ]
  R3 = Rotary Potentiometer (Small) [maximum_resistance=100kΩ]
  S3 = Toggle Switch [package=THT]

nets:
  N1: R1.Pin_0, Arduino2.GND, R2.leg2, R3.leg1
  N2: R1.Pin_1, Arduino2.D2, S3.L2
  N3: Arduino2.+5V, R2.leg1, R3.leg2, S3.COM
  N4: Arduino2.A0, R2.wiper
  N5: Arduino2.A1, R3.wiper
